// Logisim project muxrisccore.circ as structural Verilog: 1 circuit, main circuit main
module main (
);

  wire and_1_out, and_2_out, and_3_out, and_4_out, and_5_out, bitselector_9_out, bitselector_10_out,
       clock_1_out, clock_2_out, clock_3_out, clock_4_out, clock_5_out, clock_6_out, clock_7_out,
       clock_8_out, clock_9_out, clock_10_out, comparator_1_eq, comparator_3_eq, comparator_4_eq,
       comparator_5_eq, comparator_6_eq, comparator_7_eq, comparator_7_lt, comparator_8_eq, comparator_9_eq,
       comparator_9_lt, counter_1_q, counter_2_q, demultiplexer_1_out0, demultiplexer_1_out1,
       demultiplexer_1_out2, demultiplexer_1_out3, fpcomparator_1_p6, fpcomparator_1_p7, multiplexer_1_out,
       multiplexer_7_out, not_1_out, not_2_out, not_3_out, not_4_out, or_1_out, or_2_out, or_4_out, or_5_out,
       register_7_q;
  wire [1:0] bitselector_11_out;
  wire [3:0] bitselector_5_out, bitselector_6_out, bitselector_7_out, bitselector_8_out;
  wire [15:0] bitselector_1_out, bitselector_2_out, bitselector_3_out, bitselector_4_out, bitselector_12_out,
       bitselector_13_out, counter_3_q, multiplexer_3_out, multiplexer_6_out;
  wire [63:0] fpcomparator_1_p4, multiplexer_2_out, multiplexer_4_out, multiplexer_8_out, or_3_out,
       ram_1_dout, register_1_q, register_2_q, register_3_q, register_4_q, register_5_q, register_6_q;

  Register #(.width(64)) register_1 (
    .D(multiplexer_2_out), .en(demultiplexer_1_out0), .clk(clock_1_out), .Q(register_1_q));  // open: clr
  Clock clock_1 (.out(clock_1_out));
  BitSelector #(.group(16), .width(64)) bitselector_1 (.in(register_2_q), .out(bitselector_1_out), .sel(2'b11));
  BitSelector #(.group(16), .width(64)) bitselector_2 (.in(register_2_q), .out(bitselector_2_out), .sel(2'b10));
  BitSelector #(.group(16), .width(64)) bitselector_3 (.in(register_2_q), .out(bitselector_3_out), .sel(2'b01));
  BitSelector #(.group(16), .width(64)) bitselector_4 (.in(register_2_q), .out(bitselector_4_out), .sel(2'b00));
  Register #(.trigger("falling"), .width(64)) register_2 (
    .D(ram_1_dout), .en(or_1_out), .clk(clock_2_out), .Q(register_2_q));  // open: clr
  or or_1 (or_1_out, or_4_out, comparator_1_eq);
  Comparator #(.width(64)) comparator_1 (.a({64{1'b0}}), .b(register_2_q), .eq(comparator_1_eq));  // open: gt, lt
  Clock clock_2 (.out(clock_2_out));
  BitSelector #(.group(4), .width(16)) bitselector_5 (.in(bitselector_1_out), .out(bitselector_5_out), .sel(2'b00));
  BitSelector #(.group(4), .width(16)) bitselector_6 (.in(bitselector_2_out), .out(bitselector_6_out), .sel(2'b00));
  BitSelector #(.group(4), .width(16)) bitselector_7 (.in(bitselector_3_out), .out(bitselector_7_out), .sel(2'b00));
  BitSelector #(.group(4), .width(16)) bitselector_8 (.in(bitselector_4_out), .out(bitselector_8_out), .sel(2'b00));
  Register #(.width(64)) register_3 (
    .D(multiplexer_2_out), .en(demultiplexer_1_out1), .clk(clock_3_out), .Q(register_3_q));  // open: clr
  Clock clock_3 (.out(clock_3_out));
  BitSelector #(.width(64)) bitselector_9 (.in(fpcomparator_1_p4), .out(bitselector_9_out), .sel({6{1'b0}}));
  Comparator #(.mode("unsigned"), .width(4)) comparator_2 (.a(bitselector_8_out), .b(4'b0000));  // open: gt, eq, lt
  Comparator #(.mode("unsigned"), .width(4)) comparator_3 (
    .a(bitselector_8_out), .b(4'b0001), .eq(comparator_3_eq));  // open: gt, lt
  Comparator #(.mode("unsigned"), .width(4)) comparator_4 (
    .a(bitselector_8_out), .b(4'b0010), .eq(comparator_4_eq));  // open: gt, lt
  Counter #(.max('h1), .trigger("falling"), .width(1)) counter_1 (
    .count(comparator_4_eq), .Q(counter_1_q), .clk(clock_4_out), .clr(not_1_out));  // open: load, D, carry, up
  not not_1 (not_1_out, comparator_4_eq);
  Clock clock_4 (.out(clock_4_out));
  Comparator #(.mode("unsigned"), .width(4)) comparator_5 (
    .a(bitselector_8_out), .b(4'b0011), .eq(comparator_5_eq));  // open: gt, lt
  Counter #(.max('h1), .trigger("falling"), .width(1)) counter_2 (
    .count(comparator_5_eq), .Q(counter_2_q), .clk(clock_5_out), .clr(not_2_out));  // open: load, D, carry, up
  not not_2 (not_2_out, comparator_5_eq);
  Clock clock_5 (.out(clock_5_out));
  BitSelector #(.width(4)) bitselector_10 (.in(bitselector_7_out), .out(bitselector_10_out), .sel(2'b00));
  Comparator #(.mode("unsigned"), .width(4)) comparator_6 (
    .a(bitselector_8_out), .b(4'b0100), .eq(comparator_6_eq));  // open: gt, lt
  Multiplexer #(.select(2)) multiplexer_1 (
    .in0(comparator_7_eq), .in1(comparator_7_lt), .in2(fpcomparator_1_p6), .in3(fpcomparator_1_p7),
    .out(multiplexer_1_out), .sel(bitselector_11_out));
  BitSelector #(.group(2), .width(4)) bitselector_11 (.in(bitselector_7_out), .out(bitselector_11_out), .sel(1'b0));
  Comparator #(.width(64)) comparator_7 (
    .a(fpcomparator_1_p4), .b({64{1'b0}}), .eq(comparator_7_eq), .lt(comparator_7_lt));  // open: gt
  // FPComparator #(.fpwidth(64)) fpcomparator_1: pin names not known; wires that end beside it: register_2_q, bitselector_7_out, bitselector_8_out, fpcomparator_1_p4, {64{1'b0}}, fpcomparator_1_p6, fpcomparator_1_p7
  Register #(.width(64)) register_4 (
    .D(multiplexer_2_out), .en(demultiplexer_1_out2), .clk(clock_6_out), .Q(register_4_q));  // open: clr
  Clock clock_6 (.out(clock_6_out));
  Demultiplexer #(.select(4)) demultiplexer_1 (
    .out0(demultiplexer_1_out0), .out1(demultiplexer_1_out1), .out2(demultiplexer_1_out2),
    .out3(demultiplexer_1_out3), .in(or_2_out), .sel(bitselector_5_out));  // open: out4, out5, out6, out7, out8, out9, out10, out11, out12, out13, out14, out15
  and and_1 (and_1_out, bitselector_9_out, comparator_3_eq);
  or or_2 (or_2_out, comparator_8_eq, and_3_out, and_5_out);
  Comparator #(.mode("unsigned"), .width(1)) comparator_8 (
    .a(counter_1_q), .b(1'b1), .eq(comparator_8_eq));  // open: gt, lt
  and and_2 (and_2_out, comparator_5_eq, comparator_9_lt);
  and and_3 (and_3_out, comparator_9_eq, not_3_out);
  not not_3 (not_3_out, bitselector_10_out);
  Comparator #(.mode("unsigned"), .width(1)) comparator_9 (
    .a(counter_2_q), .b(1'b1), .eq(comparator_9_eq), .lt(comparator_9_lt));  // open: gt
  and and_4 (and_4_out, comparator_9_eq, bitselector_10_out);
  and and_5 (and_5_out, comparator_6_eq, multiplexer_1_out);
  assign or_3_out = 64'h1 | multiplexer_4_out;  // OR_Gate or_3, 64 bits wide
  or or_4 (or_4_out, comparator_3_eq, or_2_out, comparator_9_eq, comparator_6_eq);
  Register #(.width(64)) register_5 (
    .D(multiplexer_2_out), .en(demultiplexer_1_out3), .clk(clock_7_out), .Q(register_5_q));  // open: clr
  Clock clock_7 (.out(clock_7_out));
  Multiplexer #(.select(4), .width(64)) multiplexer_2 (
    .in0(ram_1_dout), .in1(ram_1_dout), .in2(ram_1_dout), .in3(ram_1_dout), .in4(or_3_out),
    .out(multiplexer_2_out), .sel(bitselector_8_out));  // open: in5, in6, in7, in8, in9, in10, in11, in12, in13, in14, in15
  buf or_5 (or_5_out, comparator_9_eq);  // OR_Gate
  not not_4 (not_4_out, or_5_out);
  BitSelector #(.group(16), .width(64)) bitselector_12 (.in(multiplexer_4_out), .out(bitselector_12_out), .sel(2'b00));
  Register #(.width(64)) register_6 (
    .D(fpcomparator_1_p4), .en(and_2_out), .clk(clock_8_out), .Q(register_6_q));  // open: clr
  Clock clock_8 (.out(clock_8_out));
  Register #(.width(1)) register_7 (.D(and_2_out), .en(1'b1), .clk(clock_8_out), .Q(register_7_q));  // open: clr
  Counter #(.max('hffff), .width(16)) counter_3 (
    .load(and_1_out), .D(bitselector_12_out), .count(not_4_out), .Q(counter_3_q), .clk(clock_9_out));  // open: carry, up, clr
  Clock clock_9 (.out(clock_9_out));
  Multiplexer #(.width(16)) multiplexer_3 (
    .in0(counter_3_q), .in1(bitselector_13_out), .out(multiplexer_3_out), .sel(register_7_q));
  BitSelector #(.group(16), .width(64)) bitselector_13 (.in(register_6_q), .out(bitselector_13_out), .sel(2'b00));
  Multiplexer #(.select(4), .width(64)) multiplexer_4 (
    .in0(register_1_q), .in1(register_3_q), .in2(register_4_q), .in3(register_5_q), .out(multiplexer_4_out),
    .sel(bitselector_5_out));  // open: in4, in5, in6, in7, in8, in9, in10, in11, in12, in13, in14, in15
  Multiplexer #(.select(4), .width(64)) multiplexer_5 (
    .in0(register_1_q), .in1(register_3_q), .in2(register_4_q), .in3(register_5_q), .out(fpcomparator_1_p4),
    .sel(bitselector_6_out));  // open: in4, in5, in6, in7, in8, in9, in10, in11, in12, in13, in14, in15
  Multiplexer #(.select(4), .width(16)) multiplexer_6 (
    .in0(counter_3_q), .in1(counter_3_q), .in2(counter_3_q), .in3(multiplexer_3_out), .in4(counter_3_q),
    .out(multiplexer_6_out), .sel(bitselector_8_out));  // open: in5, in6, in7, in8, in9, in10, in11, in12, in13, in14, in15
  Clock clock_10 (.out(clock_10_out));
  Multiplexer #(.select(4)) multiplexer_7 (
    .in0(1'b0), .in1(1'b0), .in2(1'b0), .in3(and_4_out), .in4(1'b0), .out(multiplexer_7_out),
    .sel(bitselector_8_out));  // open: in5, in6, in7, in8, in9, in10, in11, in12, in13, in14, in15
  Multiplexer #(.select(4), .width(64)) multiplexer_8 (
    .in0({64{1'b0}}), .in1({64{1'b0}}), .in2({64{1'b0}}), .in3(multiplexer_4_out), .in4({64{1'b0}}),
    .out(multiplexer_8_out), .sel(bitselector_8_out));  // open: in5, in6, in7, in8, in9, in10, in11, in12, in13, in14, in15
  RAM #(.addrWidth(16), .dataWidth(64), .enables("line"), .\type ("nonvolatile")) ram_1 (
    .addr(multiplexer_6_out), .we(multiplexer_7_out), .clk(clock_10_out), .din(multiplexer_8_out),
    .dout(ram_1_dout));
endmodule
